# Fritzing sketch lasertag (saved by Fritzing 0.9.3b)
breadboards: 1

parts:
  IR3 = TSOP312.., 314.. [package=THT]
  Q1 = Basic FET P-Channel [package="TO220 [THT]"]
  Bauteil1 = Arduino Nano (Rev3.0)
  IR4 = TSOP312.., 314.. [package=THT]
  Q2 = Basic FET P-Channel [package="TO220 [THT]"]
  R1 = Resistor [tolerance=±5% resistance=220 package=THT]
  R2 = Resistor [tolerance=±5% resistance=220 package=THT]
  J1 = Piezo Speaker
  LED1 = LED - 5mm [color="Red (633nm)" package="5 mm [THT]"]
  S1 = Pushbutton [package="[THT]"]
  C1 = Electrolytic Capacitor [capacitance=1µF package="100 mil [THT, electrolytic]"]

nets:
  GND: IR3.GND, Bauteil1.D11/MOSI, IR4.GND
  N1: IR3.Vs, Bauteil1.GND, IR4.Vs, J1.pin2, LED1.cathode, S1.Pin_1, S1.Pin_2, C1.-
  N2: IR3.Data, Q1.drain, Bauteil1.5V, IR4.Data, Q2.drain, C1.+
  N3: Q1.gate, J1.pin1
  N4: Q1.source, R2.Pin_0
  N5: Bauteil1.D2, S1.Pin_3, S1.Pin_4
  N6: Bauteil1.D3, R1.Pin_0
  N7: Bauteil1.D8, R2.Pin_1
  N8: Q2.gate, LED1.anode
  N9: Q2.source, R1.Pin_1

notes:
  Aufpassen mit den Beinchen.
  Abgleichen mit bestehendem Layout.
  NIEMALS SPANNUNG FALSCH ANLEGEN
